// Logisim project project3.circ as structural Verilog: 2 circuits, main circuit Control Unit
module Control_Unit (
);

  wire ADDRMODE, and_1_out, and_2_out, and_3_out, and_4_out, and_5_out, and_6_out, and_7_out, and_8_out,
       and_9_out, and_10_out, and_11_out, and_12_out, and_13_out, and_14_out, and_15_out, and_16_out,
       and_17_out, and_18_out, and_19_out, and_20_out, and_21_out, and_22_out, and_23_out, and_24_out,
       and_25_out, and_26_out, and_28_out, and_29_out, and_30_out, and_31_out, and_32_out, and_33_out,
       and_34_out, and_35_out, and_36_out, and_37_out, and_39_out, and_40_out, and_41_out, and_42_out,
       and_43_out, and_44_out, and_45_out, and_46_out, and_47_out, and_48_out, and_49_out, and_50_out,
       and_51_out, and_52_out, and_53_out, and_54_out, and_55_out, and_56_out, and_57_out, and_58_out,
       and_59_out, and_60_out, and_61_out, and_62_out, and_63_out, and_64_out, and_65_out, and_66_out,
       and_67_out, and_68_out, and_69_out, and_70_out, and_71_out, and_72_out, and_73_out, and_74_out,
       and_75_out, and_76_out, and_77_out, and_78_out, and_79_out, and_80_out, and_81_out, and_82_out,
       and_83_out, and_84_out, and_85_out, and_86_out, and_87_out, and_88_out, and_89_out, and_90_out,
       and_91_out, and_92_out, and_93_out, and_94_out, and_95_out, and_96_out, and_97_out, and_98_out,
       and_99_out, and_100_out, and_101_out, and_102_out, and_103_out, and_104_out, and_105_out, and_106_out,
       and_107_out, and_108_out, and_109_out, and_110_out, ARFARF, D00, D0A, D0B, D0C, D0D, D0E, D01, D02,
       D03, D04, D05, D06, D07, D08, D09, decoder_4_out6, decoder_4_out7, decoder_5_out6, decoder_5_out7,
       decoder_6_out6, decoder_6_out7, decoder_7_out6, decoder_7_out7, decoder_10_out0, decoder_10_out1,
       decoder_10_out2, decoder_10_out3, decoder_11_out0, decoder_11_out1, decoder_11_out2, decoder_11_out3,
       decoder_12_out6, decoder_12_out7, decoder_13_out6, decoder_13_out7, decoder_16_out6, decoder_16_out7,
       decoder_17_out6, decoder_17_out7, IR_Enable, IR_LH, Mem_clr, Mem_load, Mem_sel, Mem_str, nand_1_out,
       nand_2_out, nor_1_out, nor_2_out, not_1_out, not_2_out, not_3_out, not_4_out, not_5_out, not_6_out,
       not_7_out, not_8_out, not_9_out, not_10_out, not_11_out, not_12_out, not_13_out, not_14_out, or_1_out,
       or_2_out, or_3_out, or_4_out, or_6_out, or_7_out, SC_Reset, SR_Reset, T0, T1, T2, T3, T4, T5, T6, T7,
       xor_1_out, xor_2_out;
  wire [1:0] AR_FunSel, AR_OutCSel, AR_OutSel, IR_FunSel, MuxASel, MuxBSel, OutASel, OutBSel, OutCSel,
       RF_FunSel, RF_OutASel, RF_OutBSel, RF_OutSel;
  wire [2:0] AR_RegSel, controlled_buffer_65_out, or_5_out, or_8_out, or_9_out, or_10_out, or_11_out,
       or_12_out, or_13_out, or_14_out;
  wire [2:1] DESTREG;
  wire [3:0] ALU_FunSel, decoder_4_out3, decoder_5_out3, decoder_6_out3, decoder_8_out3, decoder_9_out3,
       decoder_14_out3, decoder_15_out3, RF_RegSel;
  wire [7:0] ADDRESS;
  wire [15:11] Instruction;

  Sequence_Counter sequence_counter_1 (
    .Reset(SC_Reset), .T0(T0), .T1(T1), .T2(T2), .T3(T3), .T4(T4), .T5(T5), .T6(T6), .T7(T7));
  and and_1 (and_1_out, D09, T3);
  // Organization organization_1: pin names not known; wires that end beside it: RF_OutASel, RF_OutBSel, RF_FunSel, RF_RegSel, MuxASel, MuxBSel, AR_OutCSel, AR_FunSel, AR_RegSel, D05, ALU_FunSel, IR_LH, IR_Enable, IR_FunSel, Mem_str, Mem_sel, Mem_load, Mem_clr, {Instruction, DESTREG, ADDRMODE, ADDRESS}
  not not_1 (not_1_out, ADDRMODE);
  and and_2 (and_2_out, D09, T2);
  and and_3 (and_3_out, and_2_out, not_1_out);
  assign AR_FunSel = and_3_out ? 2'b00 : 2'bz;  // Controlled_Buffer controlled_buffer_1
  assign AR_RegSel = and_3_out ? 3'b100 : 3'bz;  // Controlled_Buffer controlled_buffer_2
  assign MuxBSel = and_3_out ? 2'b01 : 2'bz;  // Controlled_Buffer controlled_buffer_3
  not not_2 (not_2_out, ADDRMODE);
  and and_4 (and_4_out, and_1_out, not_2_out);
  assign AR_OutSel = and_4_out ? 2'b00 : 2'bz;  // Controlled_Buffer controlled_buffer_4
  assign MuxASel = and_4_out ? 2'b01 : 2'bz;  // Controlled_Buffer controlled_buffer_5
  Decoder #(.select(2), .disabled(0)) decoder_1 (
    .out0(RF_RegSel[3]), .out1(RF_RegSel[2]), .out2(RF_RegSel[1]), .out3(RF_RegSel[0]), .sel(DESTREG),
    .en(and_4_out));
  not not_3 (not_3_out, ADDRMODE);
  and and_5 (and_5_out, D09, T3);
  and and_6 (and_6_out, and_5_out, not_3_out);
  assign SR_Reset = and_6_out ? 1'b1 : 1'bz;  // Controlled_Buffer controlled_buffer_6
  and and_7 (and_7_out, D09, T2);
  and and_8 (and_8_out, and_7_out, ADDRMODE);
  assign MuxASel = and_8_out ? 2'b00 : 2'bz;  // Controlled_Buffer controlled_buffer_7
  Decoder #(.select(2), .disabled(0)) decoder_2 (
    .out0(RF_RegSel[3]), .out1(RF_RegSel[2]), .out2(RF_RegSel[1]), .out3(RF_RegSel[0]), .sel(DESTREG),
    .en(and_8_out));
  and and_9 (and_9_out, D09, T2);
  and and_10 (and_10_out, and_9_out, ADDRMODE);
  assign SR_Reset = and_10_out ? 1'b1 : 1'bz;  // Controlled_Buffer controlled_buffer_8
  and and_11 (and_11_out, ADDRESS[7], and_12_out);
  and and_12 (and_12_out, ADDRESS[2], ADDRESS[3]);
  assign IR_LH = T0 ? 1'b0 : 1'bz;  // Controlled_Buffer controlled_buffer_9
  assign IR_Enable = T0 ? 1'b1 : 1'bz;  // Controlled_Buffer controlled_buffer_10
  assign IR_FunSel = T0 ? 2'b00 : 2'bz;  // Controlled_Buffer controlled_buffer_11
  assign Mem_load = T0 ? 1'b1 : 1'bz;  // Controlled_Buffer controlled_buffer_12
  assign Mem_str = T0 ? 1'b0 : 1'bz;  // Controlled_Buffer controlled_buffer_13
  assign Mem_sel = T0 ? 1'b0 : 1'bz;  // Controlled_Buffer controlled_buffer_14
  assign Mem_clr = T0 ? 1'b0 : 1'bz;  // Controlled_Buffer controlled_buffer_15
  assign AR_FunSel = T0 ? 2'b10 : 2'bz;  // Controlled_Buffer controlled_buffer_16
  assign AR_RegSel = T0 ? 3'b001 : 3'bz;  // Controlled_Buffer controlled_buffer_17
  assign AR_OutCSel = T0 ? 2'b10 : 2'bz;  // Controlled_Buffer controlled_buffer_18
  and and_13 (and_13_out, ADDRESS[7], nand_1_out);
  nand nand_1 (nand_1_out, ADDRESS[2], ADDRESS[3]);
  and and_14 (and_14_out, and_11_out, and_17_out);
  assign RF_RegSel = and_14_out ? 4'b0010 : 4'bz;  // Controlled_Buffer controlled_buffer_19
  and and_15 (and_15_out, D0A, T2);
  and and_16 (and_16_out, D0A, T4);
  and and_17 (and_17_out, D00, T2);
  and and_18 (and_18_out, and_13_out, and_17_out);
  or or_1 (or_1_out, and_14_out, and_18_out);
  assign RF_FunSel = or_1_out ? 2'b00 : 2'bz;  // Controlled_Buffer controlled_buffer_20
  assign OutCSel = or_1_out ? ADDRESS[6:5] : 2'bz;  // Controlled_Buffer controlled_buffer_21
  assign MuxASel = or_1_out ? 2'b10 : 2'bz;  // Controlled_Buffer controlled_buffer_22
  assign IR_LH = T1 ? 1'b1 : 1'bz;  // Controlled_Buffer controlled_buffer_23
  assign IR_Enable = T1 ? 1'b1 : 1'bz;  // Controlled_Buffer controlled_buffer_24
  assign IR_FunSel = T1 ? 2'b00 : 2'bz;  // Controlled_Buffer controlled_buffer_25
  assign Mem_load = T1 ? 1'b1 : 1'bz;  // Controlled_Buffer controlled_buffer_26
  assign Mem_str = T1 ? 1'b0 : 1'bz;  // Controlled_Buffer controlled_buffer_27
  assign Mem_sel = T1 ? 1'b0 : 1'bz;  // Controlled_Buffer controlled_buffer_28
  assign Mem_clr = T1 ? 1'b0 : 1'bz;  // Controlled_Buffer controlled_buffer_29
  assign AR_FunSel = T1 ? 2'b10 : 2'bz;  // Controlled_Buffer controlled_buffer_30
  assign AR_RegSel = T1 ? 3'b001 : 3'bz;  // Controlled_Buffer controlled_buffer_31
  assign AR_OutCSel = T1 ? 2'b10 : 2'bz;  // Controlled_Buffer controlled_buffer_32
  Decoder #(.select(5), .enable("false")) decoder_3 (
    .out0(D00), .out1(D01), .out2(D02), .out3(D03), .out4(D04), .out5(D05), .out6(D06), .out7(D07),
    .out8(D08), .out9(D09), .out10(D0A), .out11(D0B), .out12(D0C), .out13(D0D), .out14(D0E), .sel(Instruction));  // open: out15, out16, out17, out18, out19, out20, out21, out22, out23, out24, out25, out26, out27, out28, out29, out30, out31
  not not_4 (not_4_out, ADDRMODE);
  and and_19 (and_19_out, and_15_out, not_4_out);
  assign AR_FunSel = and_19_out ? 2'b00 : 2'bz;  // Controlled_Buffer controlled_buffer_33
  assign AR_RegSel = and_19_out ? 3'b100 : 3'bz;  // Controlled_Buffer controlled_buffer_34
  assign MuxBSel = and_19_out ? 2'b01 : 2'bz;  // Controlled_Buffer controlled_buffer_35
  not not_5 (not_5_out, ADDRMODE);
  and and_20 (and_20_out, and_16_out, not_5_out);
  assign SC_Reset = and_20_out ? 1'b1 : 1'bz;  // Controlled_Buffer controlled_buffer_36
  assign RF_RegSel = and_18_out ? 4'b0001 : 4'bz;  // Controlled_Buffer controlled_buffer_37
  nor nor_1 (nor_1_out, ADDRESS[5], ADDRESS[6]);
  assign IR_Enable = T2 ? 1'b0 : 1'bz;  // Controlled_Buffer controlled_buffer_38
  not not_6 (not_6_out, ADDRMODE);
  and and_21 (and_21_out, D0A, T3);
  and and_22 (and_22_out, and_21_out, not_6_out);
  assign RF_OutASel = and_22_out ? DESTREG : 2'bz;  // Controlled_Buffer controlled_buffer_39
  assign ALU_FunSel = and_22_out ? 4'b0100 : 4'bz;  // Controlled_Buffer controlled_buffer_40
  assign AR_OutCSel = and_22_out ? 2'b00 : 2'bz;  // Controlled_Buffer controlled_buffer_41
  assign Mem_sel = and_22_out ? 1'b0 : 1'bz;  // Controlled_Buffer controlled_buffer_42
  assign Mem_str = and_22_out ? 1'b1 : 1'bz;  // Controlled_Buffer controlled_buffer_43
  assign Mem_load = and_22_out ? 1'b0 : 1'bz;  // Controlled_Buffer controlled_buffer_44
  and and_23 (and_23_out, ADDRESS[4], nor_1_out);
  and and_24 (and_24_out, and_23_out, and_28_out);
  assign RF_RegSel = and_24_out ? 4'b0100 : 4'bz;  // Controlled_Buffer controlled_buffer_45
  and and_25 (and_25_out, ADDRESS[4], or_2_out);
  or or_2 (or_2_out, ADDRESS[5], ADDRESS[6]);
  and and_26 (and_26_out, and_25_out, and_28_out);
  and and_27 (SC_Reset, D00, T5);
  and and_28 (and_28_out, D00, T3);
  or or_3 (or_3_out, and_24_out, and_26_out);
  assign RF_FunSel = or_3_out ? 2'b00 : 2'bz;  // Controlled_Buffer controlled_buffer_46
  assign OutCSel = or_3_out ? ADDRESS[3:2] : 2'bz;  // Controlled_Buffer controlled_buffer_47
  assign MuxASel = or_3_out ? 2'b10 : 2'bz;  // Controlled_Buffer controlled_buffer_48
  assign RF_RegSel = and_26_out ? 4'b1000 : 4'bz;  // Controlled_Buffer controlled_buffer_49
  and and_29 (and_29_out, ADDRESS[2], ADDRESS[3]);
  and and_30 (and_30_out, ADDRESS[7], and_29_out);
  and and_31 (and_31_out, and_30_out, and_37_out);
  assign OutASel = and_31_out ? 2'b10 : 2'bz;  // Controlled_Buffer controlled_buffer_50
  and and_32 (and_32_out, ADDRESS[7], nand_2_out);
  nand nand_2 (nand_2_out, ADDRESS[2], ADDRESS[3]);
  or or_4 (or_4_out, and_31_out, and_39_out);
  not not_7 (not_7_out, ARFARF);
  and and_33 (and_33_out, not_7_out, or_4_out);
  assign OutBSel = and_33_out ? ADDRESS[3:2] : 2'bz;  // Controlled_Buffer controlled_buffer_51
  assign OutASel = ARFARF ? 2'b11 : 2'bz;  // Controlled_Buffer controlled_buffer_52
  assign OutBSel = ARFARF ? 2'b00 : 2'bz;  // Controlled_Buffer controlled_buffer_53
  and and_34 (and_34_out, D0B, T2);
  assign RF_RegSel = and_41_out ? decoder_4_out3 : 4'bz;  // Controlled_Buffer controlled_buffer_54
  assign AR_RegSel = and_41_out ? or_5_out : 3'bz;  // Controlled_Buffer controlled_buffer_55
  and and_35 (and_35_out, D0B, T3);
  and and_36 (and_36_out, and_35_out, and_42_out);
  assign SC_Reset = and_36_out ? 1'b1 : 1'bz;  // Controlled_Buffer controlled_buffer_56
  and and_37 (and_37_out, D00, T4);
  and and_38 (ARFARF, and_32_out, and_43_out);
  and and_39 (and_39_out, and_32_out, and_37_out);
  assign OutASel = and_39_out ? 2'b11 : 2'bz;  // Controlled_Buffer controlled_buffer_57
  not not_8 (not_8_out, ADDRESS[7]);
  not not_9 (not_9_out, DESTREG[2]);
  and and_40 (and_40_out, not_9_out, not_8_out);
  and and_41 (and_41_out, and_34_out, and_40_out);
  assign RF_OutSel = and_41_out ? ADDRESS[6:5] : 2'bz;  // Controlled_Buffer controlled_buffer_58
  assign ALU_FunSel = and_41_out ? 4'b0100 : 4'bz;  // Controlled_Buffer controlled_buffer_59
  assign MuxASel = and_41_out ? 2'b11 : 2'bz;  // Controlled_Buffer controlled_buffer_60
  Decoder #(.select(3), .disabled(0)) decoder_4 (
    .out0(decoder_4_out3[3]), .out1(decoder_4_out3[2]), .out2(decoder_4_out3[1]), .out3(decoder_4_out3[0]),
    .out4(or_5_out[2]), .out5(or_5_out[1]), .out6(decoder_4_out6), .out7(decoder_4_out7),
    .sel({DESTREG, ADDRMODE}), .en(and_41_out));
  not not_10 (not_10_out, ADDRESS[7]);
  not not_11 (not_11_out, DESTREG[2]);
  and and_42 (and_42_out, not_11_out, not_10_out);
  and and_43 (and_43_out, ADDRESS[4], or_6_out);
  and and_44 (and_44_out, and_37_out, and_43_out);
  assign OutBSel = and_44_out ? 2'b00 : 2'bz;  // Controlled_Buffer controlled_buffer_61
  assign MuxASel = and_37_out ? 2'b11 : 2'bz;  // Controlled_Buffer controlled_buffer_62
  assign MuxBSel = and_37_out ? 2'b11 : 2'bz;  // Controlled_Buffer controlled_buffer_63
  assign ALU_FunSel = and_37_out ? 4'b0101 : 4'bz;  // Controlled_Buffer controlled_buffer_64
  Decoder #(.select(3), .disabled(0)) decoder_5 (
    .out0(decoder_5_out3[3]), .out1(decoder_5_out3[2]), .out2(decoder_5_out3[1]), .out3(decoder_5_out3[0]),
    .out4(or_8_out[2]), .out5(or_8_out[1]), .out6(decoder_5_out6), .out7(decoder_5_out7),
    .sel(controlled_buffer_65_out), .en(and_37_out));
  assign controlled_buffer_65_out = and_37_out ? {DESTREG, ADDRMODE} : 3'bz;  // Controlled_Buffer controlled_buffer_65
  assign RF_RegSel = and_37_out ? decoder_5_out3 : 4'bz;  // Controlled_Buffer controlled_buffer_66
  assign AR_RegSel = and_37_out ? or_8_out : 3'bz;  // Controlled_Buffer controlled_buffer_67
  or or_5 (or_5_out[0], decoder_4_out6, decoder_4_out7);
  or or_6 (or_6_out, ADDRESS[5], ADDRESS[6]);
  or or_7 (or_7_out, and_44_out, and_47_out);
  or or_8 (or_8_out[0], decoder_5_out6, decoder_5_out7);
  and and_45 (and_45_out, D04, T2);
  and and_46 (and_46_out, ADDRESS[4], nor_2_out);
  and and_47 (and_47_out, and_37_out, and_46_out);
  assign OutBSel = and_47_out ? 2'b01 : 2'bz;  // Controlled_Buffer controlled_buffer_68
  not not_12 (not_12_out, ARFARF);
  and and_48 (and_48_out, or_7_out, not_12_out);
  assign OutASel = and_48_out ? ADDRESS[6:5] : 2'bz;  // Controlled_Buffer controlled_buffer_69
  and and_49 (and_49_out, and_45_out, ADDRMODE);
  assign MuxBSel = and_49_out ? 2'b01 : 2'bz;  // Controlled_Buffer controlled_buffer_70
  assign AR_RegSel = and_49_out ? 3'b001 : 3'bz;  // Controlled_Buffer controlled_buffer_71
  assign AR_FunSel = and_49_out ? 2'b00 : 2'bz;  // Controlled_Buffer controlled_buffer_72
  and and_50 (and_50_out, D04, T3);
  and and_51 (and_51_out, and_50_out, ADDRMODE);
  assign SC_Reset = and_51_out ? 1'b1 : 1'bz;  // Controlled_Buffer controlled_buffer_73
  and and_52 (and_52_out, D0B, T2);
  and and_53 (and_53_out, D0B, T3);
  nor nor_2 (nor_2_out, ADDRESS[5], ADDRESS[6]);
  and and_54 (and_54_out, and_52_out, xor_1_out);
  assign RF_OutSel = and_54_out ? ADDRESS[6:5] : 2'bz;  // Controlled_Buffer controlled_buffer_74
  assign ALU_FunSel = and_54_out ? 4'b0100 : 4'bz;  // Controlled_Buffer controlled_buffer_75
  assign MuxBSel = and_54_out ? 2'b11 : 2'bz;  // Controlled_Buffer controlled_buffer_76
  Decoder #(.select(3), .disabled(0)) decoder_6 (
    .out0(decoder_6_out3[3]), .out1(decoder_6_out3[2]), .out2(decoder_6_out3[1]), .out3(decoder_6_out3[0]),
    .out4(or_9_out[2]), .out5(or_9_out[1]), .out6(decoder_6_out6), .out7(decoder_6_out7),
    .sel({DESTREG, ADDRMODE}), .en(and_54_out));
  assign RF_RegSel = and_54_out ? decoder_6_out3 : 4'bz;  // Controlled_Buffer controlled_buffer_77
  assign AR_RegSel = and_54_out ? or_9_out : 3'bz;  // Controlled_Buffer controlled_buffer_78
  assign AR_OutCSel = and_54_out ? ADDRESS[6:5] : 2'bz;  // Controlled_Buffer controlled_buffer_79
  assign MuxASel = and_54_out ? 2'b10 : 2'bz;  // Controlled_Buffer controlled_buffer_80
  and and_55 (and_55_out, and_53_out, xor_2_out);
  assign SC_Reset = and_55_out ? 1'b1 : 1'bz;  // Controlled_Buffer controlled_buffer_81
  xor xor_1 (xor_1_out, DESTREG[2], ADDRESS[7]);
  or or_9 (or_9_out[0], decoder_6_out6, decoder_6_out7);
  xor xor_2 (xor_2_out, DESTREG[2], ADDRESS[7]);
  and and_56 (and_56_out, D05, D05, T2);
  and and_57 (and_57_out, D05, D05, T3);
  and and_58 (and_58_out, and_56_out, ADDRMODE);
  assign MuxBSel = and_58_out ? 2'b01 : 2'bz;  // Controlled_Buffer controlled_buffer_82
  assign AR_RegSel = and_58_out ? 3'b001 : 3'bz;  // Controlled_Buffer controlled_buffer_83
  assign AR_FunSel = and_58_out ? 2'b00 : 2'bz;  // Controlled_Buffer controlled_buffer_84
  and and_59 (and_59_out, and_57_out, ADDRMODE);
  assign SC_Reset = and_59_out ? 1'b1 : 1'bz;  // Controlled_Buffer controlled_buffer_85
  and and_60 (and_60_out, D0B, T2);
  and and_61 (and_61_out, D0B, T3);
  and and_62 (and_62_out, D0B, T4);
  and and_63 (and_63_out, and_62_out, and_68_out);
  and and_64 (and_64_out, DESTREG[2], ADDRESS[7]);
  and and_65 (and_65_out, and_60_out, and_64_out);
  assign AR_OutCSel = and_65_out ? ADDRESS[6:5] : 2'bz;  // Controlled_Buffer controlled_buffer_86
  assign MuxASel = and_65_out ? 2'b10 : 2'bz;  // Controlled_Buffer controlled_buffer_87
  assign RF_RegSel = and_65_out ? 4'b0001 : 4'bz;  // Controlled_Buffer controlled_buffer_88
  and and_66 (and_66_out, DESTREG[2], ADDRESS[7]);
  and and_67 (and_67_out, and_61_out, and_66_out);
  assign RF_OutASel = and_67_out ? 2'b11 : 2'bz;  // Controlled_Buffer controlled_buffer_89
  assign ALU_FunSel = and_67_out ? 4'b0100 : 4'bz;  // Controlled_Buffer controlled_buffer_90
  assign MuxBSel = and_67_out ? 2'b11 : 2'bz;  // Controlled_Buffer controlled_buffer_91
  Decoder #(.select(3), .disabled(0)) decoder_7 (
    .out4(or_10_out[2]), .out5(or_10_out[1]), .out6(decoder_7_out6), .out7(decoder_7_out7),
    .sel({DESTREG, ADDRMODE}), .en(and_67_out));  // open: out0, out1, out2, out3
  assign AR_RegSel = and_67_out ? or_10_out : 3'bz;  // Controlled_Buffer controlled_buffer_92
  and and_68 (and_68_out, DESTREG[2], ADDRESS[7]);
  assign SC_Reset = and_63_out ? 1'b1 : 1'bz;  // Controlled_Buffer controlled_buffer_93
  or or_10 (or_10_out[0], decoder_7_out6, decoder_7_out7);
  not not_13 (not_13_out, D05);
  not not_14 (not_14_out, D05);
  and and_69 (and_69_out, not_13_out, D06, T2);
  and and_70 (and_70_out, and_69_out, ADDRMODE);
  assign MuxBSel = and_70_out ? 2'b01 : 2'bz;  // Controlled_Buffer controlled_buffer_94
  assign AR_RegSel = and_70_out ? 3'b001 : 3'bz;  // Controlled_Buffer controlled_buffer_95
  assign AR_FunSel = and_70_out ? 2'b00 : 2'bz;  // Controlled_Buffer controlled_buffer_96
  and and_71 (and_71_out, not_14_out, D06, T2);
  and and_72 (and_72_out, and_71_out, ADDRMODE);
  assign SC_Reset = and_72_out ? 1'b1 : 1'bz;  // Controlled_Buffer controlled_buffer_97
  and and_73 (and_73_out, D07, T3, decoder_11_out0);
  assign SC_Reset = and_73_out ? 1'b1 : 1'bz;  // Controlled_Buffer controlled_buffer_98
  and and_74 (and_74_out, D08, T3, decoder_10_out0);
  assign SC_Reset = and_74_out ? 1'b1 : 1'bz;  // Controlled_Buffer controlled_buffer_99
  and and_75 (and_75_out, D07, T2);
  Decoder #(.select(3), .disabled(0)) decoder_8 (
    .out0(decoder_8_out3[3]), .out1(decoder_8_out3[2]), .out2(decoder_8_out3[1]), .out3(decoder_8_out3[0]),
    .sel({DESTREG, ADDRMODE}), .en(T2));  // open: out4, out5, out6, out7
  assign RF_FunSel = and_78_out ? 2'b00 : 2'bz;  // Controlled_Buffer controlled_buffer_100
  and and_76 (and_76_out, D08, T2);
  and and_77 (and_77_out, and_76_out, decoder_10_out0);
  Decoder #(.select(3), .disabled(0)) decoder_9 (
    .out0(decoder_9_out3[3]), .out1(decoder_9_out3[2]), .out2(decoder_9_out3[1]), .out3(decoder_9_out3[0]),
    .sel({DESTREG, ADDRMODE}), .en(T2));  // open: out4, out5, out6, out7
  assign RF_FunSel = and_77_out ? 2'b00 : 2'bz;  // Controlled_Buffer controlled_buffer_101
  and and_78 (and_78_out, and_75_out, decoder_11_out0);
  assign MuxASel = and_78_out ? 2'b11 : 2'bz;  // Controlled_Buffer controlled_buffer_102
  assign MuxASel = and_77_out ? 2'b11 : 2'bz;  // Controlled_Buffer controlled_buffer_103
  assign RF_RegSel = and_78_out ? decoder_8_out3 : 4'bz;  // Controlled_Buffer controlled_buffer_104
  and and_79 (and_79_out, and_82_out, decoder_10_out0);
  assign RF_OutASel = and_79_out ? ADDRESS[6:5] : 2'bz;  // Controlled_Buffer controlled_buffer_105
  assign ALU_FunSel = and_79_out ? 4'b1011 : 4'bz;  // Controlled_Buffer controlled_buffer_106
  assign RF_RegSel = and_77_out ? decoder_9_out3 : 4'bz;  // Controlled_Buffer controlled_buffer_107
  and and_80 (and_80_out, and_81_out, decoder_11_out0);
  assign RF_OutASel = and_80_out ? ADDRESS[6:5] : 2'bz;  // Controlled_Buffer controlled_buffer_108
  assign ALU_FunSel = and_80_out ? 4'b1010 : 4'bz;  // Controlled_Buffer controlled_buffer_109
  and and_81 (and_81_out, D07, T2);
  and and_82 (and_82_out, D08, T2);
  Decoder #(.select(2), .enable("false")) decoder_10 (
    .out0(decoder_10_out0), .out1(decoder_10_out1), .out2(decoder_10_out2), .out3(decoder_10_out3),
    .sel({ADDRESS[7], DESTREG[2]}));
  Decoder #(.select(2), .enable("false")) decoder_11 (
    .out0(decoder_11_out0), .out1(decoder_11_out1), .out2(decoder_11_out2), .out3(decoder_11_out3),
    .sel({ADDRESS[7], DESTREG[2]}));
  and and_83 (and_83_out, D07, T3, decoder_11_out1);
  assign AR_RegSel = and_87_out ? or_11_out : 3'bz;  // Controlled_Buffer controlled_buffer_110
  and and_84 (and_84_out, D08, T3, decoder_10_out1);
  assign SC_Reset = and_84_out ? 1'b1 : 1'bz;  // Controlled_Buffer controlled_buffer_111
  assign AR_RegSel = and_89_out ? or_12_out : 3'bz;  // Controlled_Buffer controlled_buffer_112
  assign SC_Reset = and_83_out ? 1'b1 : 1'bz;  // Controlled_Buffer controlled_buffer_113
  Decoder #(.select(3), .disabled(0), .enable("false")) decoder_12 (
    .out4(or_11_out[2]), .out5(or_11_out[1]), .out6(decoder_12_out6), .out7(decoder_12_out7),
    .sel({DESTREG, ADDRMODE}));  // open: out0, out1, out2, out3
  and and_85 (and_85_out, D07, T2);
  Decoder #(.select(3), .disabled(0), .enable("false")) decoder_13 (
    .out4(or_12_out[2]), .out5(or_12_out[1]), .out6(decoder_13_out6), .out7(decoder_13_out7),
    .sel({DESTREG, ADDRMODE}));  // open: out0, out1, out2, out3
  and and_86 (and_86_out, D08, T2);
  and and_87 (and_87_out, and_86_out, decoder_10_out1);
  or or_11 (or_11_out[0], decoder_12_out6, decoder_12_out7);
  and and_88 (and_88_out, and_81_out, decoder_11_out1);
  assign RF_OutASel = and_88_out ? ADDRESS[6:5] : 2'bz;  // Controlled_Buffer controlled_buffer_114
  assign ALU_FunSel = and_88_out ? 4'b1010 : 4'bz;  // Controlled_Buffer controlled_buffer_115
  and and_89 (and_89_out, and_85_out, decoder_11_out1);
  assign MuxBSel = and_89_out ? 2'b11 : 2'bz;  // Controlled_Buffer controlled_buffer_116
  assign AR_FunSel = and_89_out ? 2'b00 : 2'bz;  // Controlled_Buffer controlled_buffer_117
  or or_12 (or_12_out[0], decoder_13_out6, decoder_13_out7);
  and and_90 (and_90_out, and_82_out, decoder_10_out1);
  assign RF_OutASel = and_90_out ? ADDRESS[6:5] : 2'bz;  // Controlled_Buffer controlled_buffer_118
  assign ALU_FunSel = and_90_out ? 4'b1011 : 4'bz;  // Controlled_Buffer controlled_buffer_119
  assign MuxBSel = and_87_out ? 2'b11 : 2'bz;  // Controlled_Buffer controlled_buffer_120
  assign AR_FunSel = and_87_out ? 2'b00 : 2'bz;  // Controlled_Buffer controlled_buffer_121
  and and_91 (and_91_out, D07, T2);
  and and_92 (and_92_out, decoder_11_out2, and_91_out);
  Decoder #(.select(3), .disabled(0)) decoder_14 (
    .out0(decoder_14_out3[3]), .out1(decoder_14_out3[2]), .out2(decoder_14_out3[1]),
    .out3(decoder_14_out3[0]), .sel({DESTREG, ADDRMODE}), .en(T3));  // open: out4, out5, out6, out7
  and and_93 (and_93_out, D07, T4, decoder_11_out2);
  assign SC_Reset = and_93_out ? 1'b1 : 1'bz;  // Controlled_Buffer controlled_buffer_122
  and and_94 (and_94_out, D08, T2);
  and and_95 (and_95_out, decoder_10_out2, and_94_out);
  and and_96 (and_96_out, decoder_10_out2, and_100_out);
  Decoder #(.select(3), .disabled(0)) decoder_15 (
    .out0(decoder_15_out3[3]), .out1(decoder_15_out3[2]), .out2(decoder_15_out3[1]),
    .out3(decoder_15_out3[0]), .sel({DESTREG, ADDRMODE}), .en(T3));  // open: out4, out5, out6, out7
  and and_97 (and_97_out, D08, T4, decoder_10_out2);
  assign SC_Reset = and_97_out ? 1'b1 : 1'bz;  // Controlled_Buffer controlled_buffer_123
  assign AR_OutCSel = and_92_out ? ADDRESS[6:5] : 2'bz;  // Controlled_Buffer controlled_buffer_124
  assign MuxASel = and_92_out ? 2'b10 : 2'bz;  // Controlled_Buffer controlled_buffer_125
  assign RF_RegSel = and_92_out ? 4'b0001 : 4'bz;  // Controlled_Buffer controlled_buffer_126
  assign RF_FunSel = and_92_out ? 2'b00 : 2'bz;  // Controlled_Buffer controlled_buffer_127
  and and_98 (and_98_out, D07, T3);
  and and_99 (and_99_out, decoder_11_out2, and_98_out);
  assign RF_OutASel = and_99_out ? 2'b11 : 2'bz;  // Controlled_Buffer controlled_buffer_128
  assign ALU_FunSel = and_99_out ? 4'b1010 : 4'bz;  // Controlled_Buffer controlled_buffer_129
  assign MuxASel = and_99_out ? 2'b11 : 2'bz;  // Controlled_Buffer controlled_buffer_130
  assign RF_FunSel = and_99_out ? 2'b00 : 2'bz;  // Controlled_Buffer controlled_buffer_131
  assign AR_OutCSel = and_95_out ? ADDRESS[6:5] : 2'bz;  // Controlled_Buffer controlled_buffer_132
  assign MuxASel = and_95_out ? 2'b10 : 2'bz;  // Controlled_Buffer controlled_buffer_133
  assign RF_RegSel = and_95_out ? 4'b0001 : 4'bz;  // Controlled_Buffer controlled_buffer_134
  assign RF_FunSel = and_95_out ? 2'b00 : 2'bz;  // Controlled_Buffer controlled_buffer_135
  and and_100 (and_100_out, D08, T3);
  assign RF_OutASel = and_96_out ? 2'b11 : 2'bz;  // Controlled_Buffer controlled_buffer_136
  assign ALU_FunSel = and_96_out ? 4'b1011 : 4'bz;  // Controlled_Buffer controlled_buffer_137
  assign MuxASel = and_96_out ? 2'b11 : 2'bz;  // Controlled_Buffer controlled_buffer_138
  assign RF_FunSel = and_96_out ? 2'b00 : 2'bz;  // Controlled_Buffer controlled_buffer_139
  assign RF_RegSel = and_99_out ? decoder_14_out3 : 4'bz;  // Controlled_Buffer controlled_buffer_140
  assign RF_RegSel = and_96_out ? decoder_15_out3 : 4'bz;  // Controlled_Buffer controlled_buffer_141
  and and_101 (and_101_out, D07, T2);
  and and_102 (and_102_out, decoder_11_out3, and_101_out);
  and and_103 (and_103_out, decoder_11_out3, and_109_out);
  assign AR_RegSel = and_103_out ? or_13_out : 3'bz;  // Controlled_Buffer controlled_buffer_142
  and and_104 (and_104_out, D08, T2);
  and and_105 (and_105_out, decoder_10_out3, and_104_out);
  and and_106 (and_106_out, D08, T3);
  and and_107 (and_107_out, decoder_10_out3, and_106_out);
  assign RF_OutASel = and_107_out ? 2'b11 : 2'bz;  // Controlled_Buffer controlled_buffer_143
  assign ALU_FunSel = and_107_out ? 4'b1011 : 4'bz;  // Controlled_Buffer controlled_buffer_144
  assign MuxBSel = and_107_out ? 2'b11 : 2'bz;  // Controlled_Buffer controlled_buffer_145
  assign AR_FunSel = and_107_out ? 2'b00 : 2'bz;  // Controlled_Buffer controlled_buffer_146
  assign AR_RegSel = and_107_out ? or_14_out : 3'bz;  // Controlled_Buffer controlled_buffer_147
  and and_108 (and_108_out, D08, T4, decoder_10_out3);
  assign SC_Reset = and_108_out ? 1'b1 : 1'bz;  // Controlled_Buffer controlled_buffer_148
  assign AR_OutCSel = and_102_out ? ADDRESS[6:5] : 2'bz;  // Controlled_Buffer controlled_buffer_149
  assign MuxASel = and_102_out ? 2'b10 : 2'bz;  // Controlled_Buffer controlled_buffer_150
  assign RF_RegSel = and_102_out ? 4'b0001 : 4'bz;  // Controlled_Buffer controlled_buffer_151
  assign RF_FunSel = and_102_out ? 2'b00 : 2'bz;  // Controlled_Buffer controlled_buffer_152
  and and_109 (and_109_out, D07, T3);
  assign RF_OutASel = and_103_out ? 2'b11 : 2'bz;  // Controlled_Buffer controlled_buffer_153
  assign ALU_FunSel = and_103_out ? 4'b1010 : 4'bz;  // Controlled_Buffer controlled_buffer_154
  assign MuxBSel = and_103_out ? 2'b11 : 2'bz;  // Controlled_Buffer controlled_buffer_155
  assign AR_FunSel = and_103_out ? 2'b00 : 2'bz;  // Controlled_Buffer controlled_buffer_156
  Decoder #(.select(3), .disabled(0)) decoder_16 (
    .out4(or_13_out[2]), .out5(or_13_out[1]), .out6(decoder_16_out6), .out7(decoder_16_out7),
    .sel({DESTREG, ADDRMODE}), .en(T3));  // open: out0, out1, out2, out3
  and and_110 (and_110_out, D07, T4, decoder_11_out3);
  assign SC_Reset = and_110_out ? 1'b1 : 1'bz;  // Controlled_Buffer controlled_buffer_157
  assign AR_OutCSel = and_105_out ? ADDRESS[6:5] : 2'bz;  // Controlled_Buffer controlled_buffer_158
  assign MuxASel = and_105_out ? 2'b10 : 2'bz;  // Controlled_Buffer controlled_buffer_159
  assign RF_RegSel = and_105_out ? 4'b0001 : 4'bz;  // Controlled_Buffer controlled_buffer_160
  assign RF_FunSel = and_105_out ? 2'b00 : 2'bz;  // Controlled_Buffer controlled_buffer_161
  Decoder #(.select(3), .disabled(0)) decoder_17 (
    .out4(or_14_out[2]), .out5(or_14_out[1]), .out6(decoder_17_out6), .out7(decoder_17_out7),
    .sel({DESTREG, ADDRMODE}), .en(T3));  // open: out0, out1, out2, out3
  or or_13 (or_13_out[0], decoder_16_out6, decoder_16_out7);
  or or_14 (or_14_out[0], decoder_17_out6, decoder_17_out7);

  // Other names for the same wires on the sheet: Instruction[10:0] = {DESTREG, ADDRMODE, ADDRESS};
  //   SRCREG1[2:0] = ADDRESS[7:5]; SRCREG2[2:0] = ADDRESS[4:2]; DESTREG[0] = ADDRMODE; REGSEL[1:0] = DESTREG;
  //   OPCODE[4:0] = Instruction; Z = D05

  // Notes on the sheet:
  //   Sequence Counter
  //   ORGANIZATION
  //   D09 - LD
  //   FETCH & DECODE
  //   D0A - ST
  //   D00 - ADD
  //   RF TO RF
  //   D04 - BRA
  //   RF TO AR or AR TO RF
  //   D0B - MOV
  //   D05 - BEQ
  //   AR TO AR
  //   D06 - BNE
  //   D07 - LSL
  //   D08 - LSR
endmodule

module Sequence_Counter (
  input  Reset,
  output T0,
  output T1,
  output T2,
  output T3,
  output T4,
  output T5,
  output T6,
  output T7
);

  wire clock_1_out;
  wire [2:0] counter_1_q;

  Clock clock_1 (.out(clock_1_out));
  Counter #(.width(3), .max('h7)) counter_1 (
    .count(1'b1), .Q(counter_1_q), .clk(clock_1_out), .clr(Reset));  // open: load, D, carry, preset, down
  Decoder #(.select(3), .enable("false")) decoder_1 (
    .out0(T0), .out1(T1), .out2(T2), .out3(T3), .out4(T4), .out5(T5), .out6(T6), .out7(T7), .sel(counter_1_q));
endmodule
